# Fritzing sketch ESP32C3 + MP6050 + TP4056 + 5V Boost Converter (saved by Fritzing 1.0.1rc)

parts:
  A1 = XIAO ESP32C3-smd
  TP1 = TP4056 [chip_label=TP4056 package="DIP (Dual Inline) [THT]"]
  S1 = Adafruit 3104 lighted pushbutton [package=THT]
  S2 = Round Pushbutton
  NEOPIXEL2 = Neopixel Strip -- Black (30/m)
  A2 = mini boost module
  BAT1 = Battery Holders [package=battery-aa]
  Part1 = InvenSense MPU6050

nets:
  GND: A1.Pin_2, A1.Pin_21, S2.leg1, NEOPIXEL2.GND, A2.Pin_1, Part1.GND
  N1: A1.Pin_13, Part1.SDA
  N2: A1.Pin_14, Part1.SCL
  N3: A1.Pin_17, S2.leg0
  N4: A1.Pin_19, NEOPIXEL2.DI
  N5: A1.Pin_20, Part1.VCC
  N6: A1.Pin_22, NEOPIXEL2.+5V, A2.Pin_2
  N7: TP1.pin4, TP1.pin5, S1.pin_6, A2.Pin_3, BAT1.-, BAT1.+
  N8: S1.pin_5, A2.Pin_4

custom parts:
  XIAO ESP32C3-smd: Seeed Studio XIAO ESP32C3 adopts new RISC-V architecture, supporting both Wi-Fi and BLE wireless connectivities.
  TP4056: A DIP stand-in part for whatever IC you want. With 6 pins on a 300mil dual inline package (DIP) footprint.
  Adafruit 3104 lighted pushbutton: This Mini Illuminated Momentary Power Button it an adorable breadboard-friendly tactile switch that has a built-in LED. It provides a simple way to add a tactile switch and a colorful universal power symbol to your project.
  Neopixel Strip -- Black (30/m): Neopixel Strip, Black, 30 pixels per meter.
  mini boost module: mini boost module.
